// Logisim project Experimento 1 - Comparador de senhas.circ as structural Verilog: 1 circuit, main circuit main
module main (
  input  in_1,
  input  in_2,
  input  in_3,
  input  in_4,
  input  in_5,
  input  in_6,
  input  in_7,
  input  in_8
);

  wire and_1_out, xnor_1_out, xnor_2_out, xnor_3_out, xnor_4_out;

  xnor xnor_1 (xnor_1_out, in_1, in_5);
  xnor xnor_2 (xnor_2_out, in_2, in_6);
  xnor xnor_3 (xnor_3_out, in_3, in_7);
  xnor xnor_4 (xnor_4_out, in_4, in_8);
  and and_1 (and_1_out, xnor_1_out, xnor_2_out, xnor_3_out, xnor_4_out);
  LED led_1 (.in(and_1_out));

  // Notes on the sheet:
  //   Senha do Cofre
  //   Bits de Entrada do usuári
endmodule
