// Logisim project Experimento 1 - Parte 1.circ as structural Verilog: 1 circuit, main circuit main
module main (
  input  Entradas,
  input  in_2,
  input  in_3
);

  wire and_1_out;

  and and_1 (and_1_out, Entradas, in_2, in_3);
  LED led_1 (.in(and_1_out));
endmodule
