// Logisim project Experimento 1 - Parte 2.circ as structural Verilog: 1 circuit, main circuit main
module main (
  input  A,
  input  B
);

  wire nand_1_out, nand_2_out, nand_3_out, not_1_out, not_2_out;

  not not_1 (not_1_out, A);
  not not_2 (not_2_out, B);
  nand nand_1 (nand_1_out, not_1_out, not_2_out);
  nand nand_2 (nand_2_out, A, B);
  nand nand_3 (nand_3_out, nand_1_out, nand_2_out);
  LED led_1 (.in(nand_3_out));

  // Notes on the sheet:
  //   Bits de Entada
endmodule
