// Logisim project Experimento 1 - Parte 3.circ as structural Verilog: 1 circuit, main circuit main
module main (
  input  A1,
  input  B1,
  input  A2,
  input  B2,
  input  A3,
  input  B3
);

  wire and_1_out, xnor_1_out, xnor_2_out, xnor_3_out;

  xnor xnor_1 (xnor_1_out, A1, B1);
  xnor xnor_2 (xnor_2_out, A2, B2);
  xnor xnor_3 (xnor_3_out, A3, B3);
  and and_1 (and_1_out, xnor_1_out, xnor_2_out, xnor_3_out);
  LED led_1 (.in(and_1_out));

  // Notes on the sheet:
  //   Bits de Entrada
endmodule
