// Logisim project Circuito_7SEG.circ as structural Verilog: 10 circuits, main circuit decoderA
module decoderA (
  input  X3,
  input  X2,
  input  X1,
  input  X0,
  output a
);

  wire and_1_out, nor_1_out;

  nor nor_1 (nor_1_out, X3, X2, X0);
  and and_1 (and_1_out, X2, X0);
  or or_1 (a, X3, X1, nor_1_out, and_1_out);
endmodule

module decoderB (
  input  X3,
  input  X2,
  input  X1,
  input  X0,
  output b
);

  wire and_1_out, nor_1_out, nor_2_out, not_1_out;

  not not_1 (not_1_out, X3);
  nor nor_1 (nor_1_out, X3, X2);
  and and_1 (and_1_out, X1, not_1_out, X0);
  nor nor_2 (nor_2_out, X1, X0);
  or or_1 (b, X3, nor_1_out, nor_2_out, and_1_out);
endmodule

module decoderC (
  input  X3,
  input  X2,
  input  X1,
  input  X0,
  output c
);

  wire not_1_out;

  or or_1 (c, X3, X2, not_1_out, X0);
  not not_1 (not_1_out, X1);
endmodule

module decoderD (
  input  X3,
  input  X2,
  input  X1,
  input  X0,
  output d
);

  wire and_1_out, and_2_out, and_3_out, nor_1_out, not_1_out, not_2_out, not_3_out;

  nor nor_1 (nor_1_out, X2, X1, X0);
  not not_1 (not_1_out, X2);
  and and_1 (and_1_out, not_1_out, X1, X0);
  not not_2 (not_2_out, X1);
  and and_2 (and_2_out, X0, not_2_out, X2);
  and and_3 (and_3_out, X1, not_3_out);
  not not_3 (not_3_out, X0);
  or or_1 (d, nor_1_out, and_1_out, and_2_out, and_3_out);
endmodule

module decoderE (
  input  X3,
  input  X2,
  input  X1,
  input  X0,
  output e
);

  wire and_1_out, nor_1_out, not_1_out;

  not not_1 (not_1_out, X0);
  and and_1 (and_1_out, not_1_out, X1);
  nor nor_1 (nor_1_out, X2, X0);
  or or_1 (e, nor_1_out, and_1_out);
endmodule

module decoderF (
  input  X3,
  input  X2,
  input  X1,
  input  X0,
  output f
);

  wire and_1_out, and_2_out, and_3_out, not_1_out, not_2_out;

  not not_1 (not_1_out, X1);
  not not_2 (not_2_out, X0);
  and and_1 (and_1_out, X2, not_1_out);
  and and_2 (and_2_out, not_1_out, not_2_out);
  and and_3 (and_3_out, not_2_out, X2);
  or or_1 (f, X3, and_1_out, and_2_out, and_3_out);
endmodule

module decoderG (
  input  X3,
  input  X2,
  input  X1,
  input  X0,
  output g
);

  wire and_1_out, and_2_out, and_3_out, not_1_out, not_2_out, not_3_out;

  not not_1 (not_1_out, X2);
  not not_2 (not_2_out, X1);
  not not_3 (not_3_out, X0);
  and and_1 (and_1_out, not_1_out, X1);
  and and_2 (and_2_out, X2, not_2_out);
  and and_3 (and_3_out, X2, not_3_out);
  or or_1 (g, X3, and_1_out, and_2_out, and_3_out);
endmodule

module decoder7_SEG (
  input  N0,
  input  N1,
  input  N2,
  input  N3,
  input  N4,
  input  N5,
  input  N6,
  input  N7,
  input  N8,
  input  N9
);

  wire coderdecbin_1_x0, coderdecbin_1_x1, coderdecbin_1_x2, coderdecbin_1_x3, decodera_1_a, decoderb_1_b,
       decoderc_1_c, decoderd_1_d, decodere_1_e, decoderf_1_f, decoderg_1_g;

  coderDecBin coderdecbin_1 (
    .N9(N9), .N8(N8), .N7(N7), .N6(N6), .N5(N5), .N4(N4), .N3(N3), .N2(N2), .N1(N1), .N0(N0),
    .X3(coderdecbin_1_x3), .X2(coderdecbin_1_x2), .X1(coderdecbin_1_x1), .X0(coderdecbin_1_x0));
  decoderA decodera_1 (
    .X3(coderdecbin_1_x3), .X2(coderdecbin_1_x2), .X1(coderdecbin_1_x1), .X0(coderdecbin_1_x0),
    .a(decodera_1_a));
  decoderB decoderb_1 (
    .X3(coderdecbin_1_x3), .X2(coderdecbin_1_x2), .X1(coderdecbin_1_x1), .X0(coderdecbin_1_x0),
    .b(decoderb_1_b));
  decoderC decoderc_1 (
    .X3(coderdecbin_1_x3), .X2(coderdecbin_1_x2), .X1(coderdecbin_1_x1), .X0(coderdecbin_1_x0),
    .c(decoderc_1_c));
  decoderD decoderd_1 (
    .X3(coderdecbin_1_x3), .X2(coderdecbin_1_x2), .X1(coderdecbin_1_x1), .X0(coderdecbin_1_x0),
    .d(decoderd_1_d));
  decoderE decodere_1 (
    .X3(coderdecbin_1_x3), .X2(coderdecbin_1_x2), .X1(coderdecbin_1_x1), .X0(coderdecbin_1_x0),
    .e(decodere_1_e));
  decoderF decoderf_1 (
    .X3(coderdecbin_1_x3), .X2(coderdecbin_1_x2), .X1(coderdecbin_1_x1), .X0(coderdecbin_1_x0),
    .f(decoderf_1_f));
  decoderG decoderg_1 (
    .X3(coderdecbin_1_x3), .X2(coderdecbin_1_x2), .X1(coderdecbin_1_x1), .X0(coderdecbin_1_x0),
    .g(decoderg_1_g));
  _7_Segment_Display u_7_segment_display_1 (
    .g(decoderg_1_g), .f(decoderf_1_f), .a(decodera_1_a), .b(decoderb_1_b), .e(decodere_1_e),
    .d(decoderd_1_d), .c(decoderc_1_c));  // open: dp
endmodule

module coderDecBin (
  input  N9,
  input  N8,
  input  N7,
  input  N6,
  input  N5,
  input  N4,
  input  N3,
  input  N2,
  input  N1,
  input  N0,
  output X3,
  output X2,
  output X1,
  output X0
);

  or or_1 (X0, N1, N3, N5, N7, N9);
  or or_2 (X1, N2, N3, N6, N7);
  or or_3 (X2, N4, N5, N6, N7);
  or or_4 (X3, N8, N9);
endmodule

module decoder_7_Seg (
  input  X3,
  input  X2,
  input  X1,
  input  X0,
  output A,
  output B,
  output C,
  output D,
  output E,
  output F,
  output G
);

  decoderA decodera_1 (.X3(X3), .X2(X2), .X1(X1), .X0(X0), .a(A));
  decoderB decoderb_1 (.X3(X3), .X2(X2), .X1(X1), .X0(X0), .b(B));
  decoderC decoderc_1 (.X3(X3), .X2(X2), .X1(X1), .X0(X0), .c(C));
  decoderD decoderd_1 (.X3(X3), .X2(X2), .X1(X1), .X0(X0), .d(D));
  decoderE decodere_1 (.X3(X3), .X2(X2), .X1(X1), .X0(X0), .e(E));
  decoderF decoderf_1 (.X3(X3), .X2(X2), .X1(X1), .X0(X0), .f(F));
  decoderG decoderg_1 (.X3(X3), .X2(X2), .X1(X1), .X0(X0), .g(G));
endmodule
