// Logisim project codificador_binario.circ as structural Verilog: 2 circuits, main circuit main
module main (
  input  X7,
  input  X6,
  input  X5,
  input  X4,
  input  X3,
  input  X2,
  input  X1,
  input  X0,
  output Z2,
  output Z1,
  output Z0
);

  or or_1 (Z2, X4, X5, X6, X7);
  or or_2 (Z1, X2, X3, X6, X7);
  or or_3 (Z0, X1, X3, X5, X7);
endmodule

module a (
);

  main main_1 ();  // open: X7, X6, X5, X4, X3, X2, X1, X0, Z2, Z1, Z0

  // Notes on the sheet:
  //   Codificador Binário 8:3
endmodule
