// Logisim project conversor_johnson.circ as structural Verilog: 2 circuits, main circuit main
module main (
  input  X2,
  input  X1,
  input  X0,
  output Y3,
  output Y2,
  output Y1,
  output Y0
);

  wire and_1_out, and_2_out, and_3_out, and_4_out, and_5_out, and_6_out, not_1_out, not_2_out, not_3_out,
       not_4_out, not_5_out, not_6_out, not_7_out;

  and and_1 (and_1_out, X0, X1, not_1_out);
  not not_1 (not_1_out, X2);
  and and_2 (and_2_out, X2, not_2_out);
  not not_2 (not_2_out, X1);
  and and_3 (and_3_out, X2, not_3_out);
  not not_3 (not_3_out, X0);
  xor xor_1 (Y1, X1, X2);
  not not_4 (not_4_out, X0);
  not not_5 (not_5_out, X1);
  and and_4 (and_4_out, not_4_out, not_5_out, X2);
  and and_5 (and_5_out, X0, not_6_out);
  not not_6 (not_6_out, X2);
  and and_6 (and_6_out, X1, not_7_out);
  not not_7 (not_7_out, X2);
  or or_1 (Y2, and_1_out, and_2_out, and_3_out);
  or or_2 (Y0, and_4_out, and_5_out, and_6_out);

  assign Y3 = X2;
endmodule

module bl (
);

  main main_1 ();  // open: X2, X1, X0, Y3, Y2, Y1, Y0

  // Notes on the sheet:
  //   Conversor de Código Johnson 3:4
endmodule
