// Logisim project decodificador_binario.circ as structural Verilog: 2 circuits, main circuit main
module main (
  input  Habilitador,
  input  A1,
  input  A0,
  output Z3,
  output Z2,
  output Z1,
  output Z0
);

  wire not_1_out, not_2_out;

  not not_1 (not_1_out, A1);
  not not_2 (not_2_out, A0);
  and and_1 (Z3, A0, Habilitador, A1);
  and and_2 (Z2, not_2_out, Habilitador, A1);
  and and_3 (Z1, A0, Habilitador, not_1_out);
  and and_4 (Z0, not_2_out, Habilitador, not_1_out);
endmodule

module a (
);

  main main_1 ();  // open: Habilitador, A1, A0, Z3, Z2, Z1, Z0

  // Notes on the sheet:
  //   Decodificador 2:4
endmodule
