// Logisim project Demux_4x1.circ as structural Verilog: 2 circuits, main circuit main
module main (
  input  S1,
  input  S0,
  input  E,
  output D0,
  output D1,
  output D2,
  output D3
);

  wire not_1_out, not_2_out;

  not not_1 (not_1_out, S1);
  not not_2 (not_2_out, S0);
  and and_1 (D0, E, not_2_out, not_1_out);
  and and_2 (D1, E, not_1_out, S0);
  and and_3 (D2, E, not_2_out, S1);
  and and_4 (D3, E, S0, S1);
endmodule

module Teste_1x8 (
  input  E,
  input  [2:0] S,
  output D0,
  output D1,
  output D2,
  output D3,
  output D4,
  output D5,
  output D6,
  output D7
);

  Demultiplexer #(.enable("false"), .select(3)) demultiplexer_1 (
    .out0(D0), .out1(D1), .out2(D2), .out3(D3), .out4(D4), .out5(D5), .out6(D6), .out7(D7), .in(E), .sel(S));
endmodule
