// Logisim project Mux_8x1.circ as structural Verilog: 3 circuits, main circuit main
module main (
  input  S,
  input  D0,
  input  D1,
  input  D2,
  input  D3,
  input  D4,
  input  D5,
  input  D6,
  input  D7,
  input  C,
  input  B,
  input  A,
  output Y,
  output W
);

  wire and_1_out, and_2_out, and_3_out, and_4_out, and_5_out, and_6_out, and_7_out, and_8_out, not_1_out,
       not_2_out, not_3_out, not_4_out, or_1_out, or_2_out;

  not not_1 (not_1_out, A);
  not not_2 (not_2_out, B);
  not not_3 (not_3_out, C);
  not not_4 (not_4_out, S);
  and and_1 (and_1_out, not_4_out, not_1_out, not_2_out, not_3_out, D0);
  and and_2 (and_2_out, not_4_out, A, not_2_out, not_3_out, D1);
  and and_3 (and_3_out, not_4_out, not_1_out, B, not_3_out, D2);
  and and_4 (and_4_out, not_4_out, A, B, not_3_out, D3);
  and and_5 (and_5_out, not_4_out, not_1_out, not_2_out, C, D4);
  and and_6 (and_6_out, not_4_out, A, not_2_out, C, D5);
  and and_7 (and_7_out, not_4_out, not_1_out, B, C, D6);
  and and_8 (and_8_out, not_4_out, A, B, C, D7);
  or or_1 (or_1_out, and_1_out, and_2_out, and_3_out, and_4_out);
  or or_2 (or_2_out, and_5_out, and_6_out, and_7_out, and_8_out);
  or or_3 (Y, or_1_out, or_2_out);
  not not_5 (W, Y);
endmodule

module BlocoLogico (
  input  D0,
  input  D1,
  input  D2,
  input  D3,
  input  D4,
  input  D5,
  input  D6,
  input  D7,
  input  D8,
  input  D9,
  input  D10,
  input  D11,
  input  D12,
  input  D13,
  input  D14,
  input  D15,
  input  [3:0] Selecao,
  input  Habilitador,
  output Y
);

  wire not_1_out;

  not not_1 (not_1_out, Habilitador);
  Multiplexer #(.select(4)) multiplexer_1 (
    .in0(D0), .in1(D1), .in2(D2), .in3(D3), .in4(D4), .in5(D5), .in6(D6), .in7(D7), .in8(D8), .in9(D9),
    .in10(D10), .in11(D11), .in12(D12), .in13(D13), .in14(D14), .in15(D15), .out(Y), .sel(Selecao),
    .en(not_1_out));
endmodule

module Mux_16x1 (
  input  C1,
  input  C0,
  input  D0,
  input  D1,
  input  D2,
  input  D3,
  input  C3,
  input  C2,
  input  D4,
  input  D5,
  input  D6,
  input  D7,
  input  D8,
  input  D9,
  input  D10,
  input  D11,
  input  D12,
  input  D13,
  input  D14,
  input  D15,
  output S
);

  wire and_1_out, and_2_out, and_3_out, and_4_out, and_5_out, and_6_out, and_7_out, and_8_out, and_9_out,
       and_10_out, and_11_out, and_12_out, and_13_out, and_14_out, and_15_out, and_16_out, and_17_out,
       and_18_out, and_19_out, and_20_out, not_1_out, not_2_out, not_3_out, not_4_out, not_5_out, not_6_out,
       not_7_out, not_8_out, not_9_out, not_10_out, or_1_out, or_2_out, or_3_out, or_4_out;

  not not_1 (not_1_out, C1);
  not not_2 (not_2_out, C1);
  not not_3 (not_3_out, C1);
  not not_4 (not_4_out, C1);
  not not_5 (not_5_out, C0);
  not not_6 (not_6_out, C0);
  not not_7 (not_7_out, C0);
  not not_8 (not_8_out, C0);
  and and_1 (and_1_out, D0, not_5_out, not_1_out);
  and and_2 (and_2_out, D1, C0, not_1_out);
  and and_3 (and_3_out, D2, not_5_out, C1);
  and and_4 (and_4_out, D3, C0, C1);
  and and_5 (and_5_out, D4, not_6_out, not_2_out);
  and and_6 (and_6_out, D5, C0, not_2_out);
  and and_7 (and_7_out, D6, not_6_out, C1);
  and and_8 (and_8_out, D7, C0, C1);
  and and_9 (and_9_out, D8, not_7_out, not_3_out);
  and and_10 (and_10_out, D9, C0, not_3_out);
  and and_11 (and_11_out, D10, not_7_out, C1);
  and and_12 (and_12_out, D11, C0, C1);
  and and_13 (and_13_out, D12, not_8_out, not_4_out);
  and and_14 (and_14_out, D13, C0, not_4_out);
  and and_15 (and_15_out, D14, not_8_out, C1);
  and and_16 (and_16_out, D15, C0, C1);
  or or_1 (or_1_out, and_1_out, and_2_out, and_3_out, and_4_out);
  or or_2 (or_2_out, and_5_out, and_6_out, and_7_out, and_8_out);
  or or_3 (or_3_out, and_9_out, and_10_out, and_11_out, and_12_out);
  or or_4 (or_4_out, and_13_out, and_14_out, and_15_out, and_16_out);
  not not_9 (not_9_out, C3);
  not not_10 (not_10_out, C2);
  and and_17 (and_17_out, or_1_out, not_10_out, not_9_out);
  and and_18 (and_18_out, or_2_out, C2, not_9_out);
  and and_19 (and_19_out, or_3_out, not_10_out, C3);
  and and_20 (and_20_out, or_4_out, C2, C3);
  or or_5 (S, and_17_out, and_18_out, and_19_out, and_20_out);
endmodule
