// Logisim project DetectorOverflow.circ as structural Verilog: 1 circuit, main circuit main
module main (
  input  S,
  input  A,
  input  B,
  output Erro
);

  wire and_1_out, and_2_out, not_1_out, not_2_out, not_3_out;

  not not_1 (not_1_out, A);
  not not_2 (not_2_out, B);
  not not_3 (not_3_out, S);
  and and_1 (and_1_out, not_1_out, not_2_out, S);
  and and_2 (and_2_out, A, B, not_3_out);
  or or_1 (Erro, and_1_out, and_2_out);
endmodule
