// Logisim project FullAdder1bit.circ as structural Verilog: 6 circuits, main circuit FullAdder1bit
module FullAdder1bit (
  input  A,
  input  B,
  input  Te,
  output S,
  output Ts
);

  wire and_1_out, and_2_out, xor_1_out;

  xor xor_1 (xor_1_out, A, B);
  xor xor_2 (S, xor_1_out, Te);
  and and_1 (and_1_out, xor_1_out, Te);
  and and_2 (and_2_out, A, B);
  or or_1 (Ts, and_1_out, and_2_out);
endmodule

module FullAdder4bit (
  input  A3,
  input  A2,
  input  A1,
  input  A0,
  input  B3,
  input  B2,
  input  B1,
  input  B0,
  input  Te,
  output S2,
  output S0,
  output S3,
  output S1,
  output TS
);

  wire and_1_out, and_2_out, and_3_out, and_4_out, and_5_out, and_6_out, and_7_out, and_8_out, or_2_out,
       or_3_out, or_4_out, xor_2_out, xor_4_out, xor_6_out, xor_8_out;

  xor xor_1 (S3, xor_2_out, or_2_out);
  or or_1 (TS, and_1_out, and_2_out);
  xor xor_2 (xor_2_out, A3, B3);
  and and_1 (and_1_out, xor_2_out, or_2_out);
  and and_2 (and_2_out, A3, B3);
  xor xor_3 (S2, xor_4_out, or_3_out);
  or or_2 (or_2_out, and_3_out, and_4_out);
  and and_3 (and_3_out, xor_4_out, or_3_out);
  and and_4 (and_4_out, A2, B2);
  xor xor_4 (xor_4_out, A2, B2);
  xor xor_5 (S1, xor_6_out, or_4_out);
  or or_3 (or_3_out, and_5_out, and_6_out);
  and and_5 (and_5_out, xor_6_out, or_4_out);
  and and_6 (and_6_out, A1, B1);
  xor xor_6 (xor_6_out, A1, B1);
  xor xor_7 (S0, xor_8_out, Te);
  or or_4 (or_4_out, and_7_out, and_8_out);
  xor xor_8 (xor_8_out, A0, B0);
  and and_7 (and_7_out, xor_8_out, Te);
  and and_8 (and_8_out, A0, B0);
endmodule

module FullAdder4bitSimplified (
  input  Te,
  input  A3,
  input  A2,
  input  A1,
  input  A0,
  input  B3,
  input  B2,
  input  B1,
  input  B0,
  output S3,
  output S2,
  output S1,
  output S0,
  output Ts
);

  wire adder_2_cout, adder_3_cout, adder_4_cout;

  Adder #(.width(1)) adder_1 (.a(A3), .b(B3), .out(S3), .cin(adder_2_cout), .cout(Ts));
  Adder #(.width(1)) adder_2 (.a(A2), .b(B2), .out(S2), .cin(adder_3_cout), .cout(adder_2_cout));
  Adder #(.width(1)) adder_3 (.a(A1), .b(B1), .out(S1), .cin(adder_4_cout), .cout(adder_3_cout));
  Adder #(.width(1)) adder_4 (.a(A0), .b(B0), .out(S0), .cin(Te), .cout(adder_4_cout));
endmodule

module IgualdadeComplemento1 (
  input  SEL,
  input  B3,
  input  B2,
  input  B1,
  input  B0,
  output Z3,
  output Z2,
  output Z1,
  output Z0
);

  xor xor_1 (Z3, B3, SEL);
  xor xor_2 (Z2, B2, SEL);
  xor xor_3 (Z1, B1, SEL);
  xor xor_4 (Z0, B0, SEL);
endmodule

module DetectorOverflow (
  input  S,
  input  A,
  input  B,
  output Erro
);

  wire and_1_out, and_2_out, not_1_out, not_2_out, not_3_out;

  not not_1 (not_1_out, A);
  not not_2 (not_2_out, B);
  not not_3 (not_3_out, S);
  and and_1 (and_1_out, not_1_out, not_2_out, S);
  and and_2 (and_2_out, A, B, not_3_out);
  or or_1 (Erro, and_1_out, and_2_out);
endmodule

module SomadorSubtrator4bits (
  input  B3,
  input  B2,
  input  B1,
  input  B0,
  input  SEL,
  input  A3,
  input  A2,
  input  A1,
  input  A0,
  output S3,
  output S2,
  output S1,
  output S0,
  output Ts,
  output Erro
);

  wire fulladder1bit_1_ts, fulladder1bit_2_ts, fulladder1bit_3_ts, fulladder1bit_4_ts,
       igualdadecomplemento1_1_z0, igualdadecomplemento1_1_z1, igualdadecomplemento1_1_z2,
       igualdadecomplemento1_1_z3;

  IgualdadeComplemento1 igualdadecomplemento1_1 (
    .SEL(SEL), .B3(B3), .B2(B2), .B1(B1), .B0(B0), .Z3(igualdadecomplemento1_1_z3),
    .Z2(igualdadecomplemento1_1_z2), .Z1(igualdadecomplemento1_1_z1), .Z0(igualdadecomplemento1_1_z0));
  FullAdder1bit fulladder1bit_1 (.A(A0), .B(igualdadecomplemento1_1_z0), .Te(SEL), .S(S0), .Ts(fulladder1bit_1_ts));
  FullAdder1bit fulladder1bit_2 (
    .A(A1), .B(igualdadecomplemento1_1_z1), .Te(fulladder1bit_1_ts), .S(S1), .Ts(fulladder1bit_2_ts));
  FullAdder1bit fulladder1bit_3 (
    .A(A2), .B(igualdadecomplemento1_1_z2), .Te(fulladder1bit_2_ts), .S(S2), .Ts(fulladder1bit_3_ts));
  FullAdder1bit fulladder1bit_4 (
    .A(A3), .B(igualdadecomplemento1_1_z3), .Te(fulladder1bit_3_ts), .S(S3), .Ts(fulladder1bit_4_ts));
  DetectorOverflow detectoroverflow_1 (.S(S3), .A(A3), .B(igualdadecomplemento1_1_z3), .Erro(Erro));
  xor xor_1 (Ts, SEL, fulladder1bit_4_ts);
endmodule
