// Logisim project SeletorIgC1.circ as structural Verilog: 1 circuit, main circuit main
module main (
  input  SEL,
  input  B3,
  input  B2,
  input  B1,
  input  B0,
  output Z3,
  output Z2,
  output Z1,
  output Z0
);

  xor xor_1 (Z3, B3, SEL);
  xor xor_2 (Z2, B2, SEL);
  xor xor_3 (Z1, B1, SEL);
  xor xor_4 (Z0, B0, SEL);
endmodule
