// Logisim project matricula.circ as structural Verilog: 2 circuits, main circuit main
module main (
  input  [3:0] in_1,
  input  [2:0] SelecaoCadeira,
  input  Clock,
  input  Clear
);

  wire adder_1_cout, not_1_out, verificadorlimites_1_maximo, verificadorlimites_1_minimo;
  wire [3:0] adder_1_out, multiplexer_1_out, multiplexer_2_out, register_1_q, verificadorlimites_1_saida;

  Multiplexer #(.enable("false"), .select(3), .width(4)) multiplexer_1 (
    .in0(4'b0001), .in1(4'b0001), .in2(4'b0001), .in3(4'b0001), .in4(4'b0100), .in5(4'b0100), .in6(4'b0100),
    .in7(4'b0100), .out(multiplexer_1_out), .sel(SelecaoCadeira));
  Adder #(.width(4)) adder_1 (
    .a(multiplexer_1_out), .b(multiplexer_2_out), .out(adder_1_out), .cin(1'b0), .cout(adder_1_cout));
  Multiplexer #(.enable("false"), .width(4)) multiplexer_2 (
    .in0(register_1_q), .in1(in_1), .out(multiplexer_2_out), .sel(verificadorlimites_1_maximo));
  verificadorLimites verificadorlimites_1 (
    .ValorAtual(multiplexer_2_out), .ValorAposCadeira(adder_1_out), .Minimo(verificadorlimites_1_minimo),
    .Maximo(verificadorlimites_1_maximo), .Saida(verificadorlimites_1_saida));
  LED MinimoNaoAtingido (.in(verificadorlimites_1_minimo));
  Register #(.width(4)) register_1 (
    .D(verificadorlimites_1_saida), .en(not_1_out), .clk(Clock), .Q(register_1_q), .clr(Clear));
  not not_1 (not_1_out, verificadorlimites_1_maximo);
  LED MaximoAtingido (.in(verificadorlimites_1_maximo));
  // also tied to GND on the sheet: adder_1_cout

  // Notes on the sheet:
  //   011: Lab. Dispositivos Eletronicos
  //   000: Experimental 1
  //   001: Experimental 2
  //   010: Lab. Sistemas Eletricos
  //   100: Calculo 1
  //   101: Calculo 2
  //   110: Calculo 3
  //   111: Mecanica 1
endmodule

module verificadorLimites (
  input  [3:0] ValorAtual,
  input  [3:0] ValorAposCadeira,
  output Minimo,
  output Maximo,
  output [3:0] Saida
);

  wire and_1_out, and_2_out, not_1_out, not_2_out, not_3_out;

  not not_1 (not_1_out, ValorAtual[3]);
  not not_2 (not_2_out, ValorAtual[2]);
  not not_3 (not_3_out, ValorAtual[1]);
  and and_1 (and_1_out, not_1_out, not_2_out);
  and and_2 (and_2_out, not_1_out, not_3_out);
  and and_3 (Maximo, ValorAtual[3], ValorAtual[2]);
  or or_1 (Minimo, and_1_out, and_2_out);

  assign Saida = ValorAposCadeira;
endmodule
